// Digital circuit Quiz2_03.dig as structural Verilog
module Quiz2_03 (
  input  reset,
  input  [7:0] N,
  input  \new ,
  input  clock,
  output [7:0] num_inc,
  output [7:0] max,
  output busy
);

  wire _00, and_1_out, gt, multiplexer_3_out, or_1_out, Q;
  wire [7:0] add_1_s, multiplexer_1_out, multiplexer_2_out, multiplexer_4_out, multiplexer_5_out, val;

  Comparator #(.Bits(8)) comparator_1 (.a(val), .b(max), .gt(gt));  // open: eq, lt
  Multiplexer #(.Bits(8)) multiplexer_1 (.sel(gt), .in_0({8{1'b0}}), .in_1(8'h1), .out(multiplexer_1_out));
  Multiplexer #(.Bits(8)) multiplexer_2 (.sel(busy), .in_0(max), .in_1(val), .out(multiplexer_2_out));
  Add #(.Bits(8)) add_1 (.a(num_inc), .b(multiplexer_1_out), .c_i(1'b0), .s(add_1_s));  // open: c_o
  Multiplexer multiplexer_3 (.sel(Q), .in_0(gt), .in_1(1'b0), .out(multiplexer_3_out));
  Multiplexer #(.Bits(8)) multiplexer_4 (
    .sel(reset), .in_0(multiplexer_2_out), .in_1({8{1'b0}}), .out(multiplexer_4_out));
  or or_1 (or_1_out, reset, busy);
  and and_1 (and_1_out, ~reset, multiplexer_3_out);  // And
  Multiplexer #(.Bits(8)) multiplexer_5 (.sel(reset), .in_0(add_1_s), .in_1({8{1'b0}}), .out(multiplexer_5_out));
  D_FF d_ff_1 (.D(and_1_out), .C(clock), .Q(Q));  // open: nQ
  Decoder decoder_1 (.sel(Q), .out_0(_00), .out_1(busy));
  Register #(.Bits(8)) register_1 (.D(multiplexer_4_out), .C(clock), .en(or_1_out), .Q(max));
  Register #(.Bits(8)) register_2 (.D(multiplexer_5_out), .C(clock), .en(or_1_out), .Q(num_inc));
  Register #(.Bits(8)) register_3 (.D(N), .C(clock), .en(\new ), .Q(val));

  // Other names for the same wires on the sheet: _01 = busy; clk = clock; cnt[7:0] = num_inc; mx[7:0] = max
endmodule

/* Test case T06:
N new reset clock num_inc max busy
0 0 1 0 x x x
0 0 1 1 0 0 0
131 1 0 0 x x x
131 1 0 1 x x x
0 0 0 0 x x x
0 0 0 1 x x x
0 0 0 0 x x x
0 0 0 1 x x x
0 0 0 0 x x x
0 0 0 1 x x x
0 0 0 0 x x x
0 0 0 1 x x x
0 0 0 0 x x x
0 0 0 1 x x x
0 0 0 0 x x x
0 0 0 1 x x x
0 0 0 0 x x x
0 0 0 1 x x x
0 0 0 0 x x x
0 0 0 1 x x x
0 0 0 0 x x x
0 0 0 1 x x x
0 0 0 0 x x x
0 0 0 1 x x x
0 0 0 0 x x x
0 0 0 1 x x x
0 0 0 0 x x x
0 0 0 1 x x x
0 0 0 0 x x x
0 0 0 1 x x x
0 0 0 0 x x x
0 0 0 1 x x x
0 0 0 0 x x x
0 0 0 1 x x x
0 0 0 0 x x x
0 0 0 1 x x x
0 0 0 0 x x x
0 0 0 1 x x x
0 0 0 0 x x x
0 0 0 1 x x x
0 0 0 0 x x x
0 0 0 1 x x x
0 0 0 0 x x x
0 0 0 1 x x x
0 0 0 0 x x x
0 0 0 1 x x x
0 0 0 0 x x x
0 0 0 1 x x x
0 0 0 0 x x x
0 0 0 1 x x x
0 0 0 0 x x x
0 0 0 1 x x x
0 0 0 0 x x x
0 0 0 1 x x x
0 0 0 0 x x x
0 0 0 1 x x x
0 0 0 0 x x x
0 0 0 1 x x x
0 0 0 0 x x x
0 0 0 1 x x x
0 0 0 0 x x x
0 0 0 1 x x x
0 0 0 0 x x x
0 0 0 1 x x x
0 0 0 0 1 131 0
0 0 0 1 1 131 0
130 1 0 0 x x x
130 1 0 1 x x x
0 0 0 0 x x x
0 0 0 1 x x x
0 0 0 0 x x x
0 0 0 1 x x x
0 0 0 0 x x x
0 0 0 1 x x x
0 0 0 0 x x x
0 0 0 1 x x x
0 0 0 0 x x x
0 0 0 1 x x x
0 0 0 0 x x x
0 0 0 1 x x x
0 0 0 0 x x x
0 0 0 1 x x x
0 0 0 0 x x x
0 0 0 1 x x x
0 0 0 0 x x x
0 0 0 1 x x x
0 0 0 0 x x x
0 0 0 1 x x x
0 0 0 0 x x x
0 0 0 1 x x x
0 0 0 0 x x x
0 0 0 1 x x x
0 0 0 0 x x x
0 0 0 1 x x x
0 0 0 0 x x x
0 0 0 1 x x x
0 0 0 0 x x x
0 0 0 1 x x x
0 0 0 0 x x x
0 0 0 1 x x x
0 0 0 0 x x x
0 0 0 1 x x x
0 0 0 0 x x x
0 0 0 1 x x x
0 0 0 0 x x x
0 0 0 1 x x x
0 0 0 0 x x x
0 0 0 1 x x x
0 0 0 0 x x x
0 0 0 1 x x x
0 0 0 0 x x x
0 0 0 1 x x x
0 0 0 0 x x x
0 0 0 1 x x x
0 0 0 0 x x x
0 0 0 1 x x x
0 0 0 0 x x x
0 0 0 1 x x x
0 0 0 0 x x x
0 0 0 1 x x x
0 0 0 0 x x x
0 0 0 1 x x x
0 0 0 0 x x x
0 0 0 1 x x x
0 0 0 0 x x x
0 0 0 1 x x x
0 0 0 0 x x x
0 0 0 1 x x x
0 0 0 0 1 131 0
0 0 0 1 1 131 0
58 1 0 0 x x x
58 1 0 1 x x x
0 0 0 0 x x x
0 0 0 1 x x x
0 0 0 0 x x x
0 0 0 1 x x x
0 0 0 0 x x x
0 0 0 1 x x x
0 0 0 0 x x x
0 0 0 1 x x x
0 0 0 0 x x x
0 0 0 1 x x x
0 0 0 0 x x x
0 0 0 1 x x x
0 0 0 0 x x x
0 0 0 1 x x x
0 0 0 0 x x x
0 0 0 1 x x x
0 0 0 0 x x x
0 0 0 1 x x x
0 0 0 0 x x x
0 0 0 1 x x x
0 0 0 0 x x x
0 0 0 1 x x x
0 0 0 0 x x x
0 0 0 1 x x x
0 0 0 0 x x x
0 0 0 1 x x x
0 0 0 0 x x x
0 0 0 1 x x x
0 0 0 0 x x x
0 0 0 1 x x x
0 0 0 0 x x x
0 0 0 1 x x x
0 0 0 0 x x x
0 0 0 1 x x x
0 0 0 0 x x x
0 0 0 1 x x x
0 0 0 0 x x x
0 0 0 1 x x x
0 0 0 0 x x x
0 0 0 1 x x x
0 0 0 0 x x x
0 0 0 1 x x x
0 0 0 0 x x x
0 0 0 1 x x x
0 0 0 0 x x x
0 0 0 1 x x x
0 0 0 0 x x x
0 0 0 1 x x x
0 0 0 0 x x x
0 0 0 1 x x x
0 0 0 0 x x x
0 0 0 1 x x x
0 0 0 0 x x x
0 0 0 1 x x x
0 0 0 0 x x x
0 0 0 1 x x x
0 0 0 0 x x x
0 0 0 1 x x x
0 0 0 0 x x x
0 0 0 1 x x x
0 0 0 0 1 131 0
0 0 0 1 1 131 0
154 1 0 0 x x x
154 1 0 1 x x x
0 0 0 0 x x x
0 0 0 1 x x x
0 0 0 0 x x x
0 0 0 1 x x x
0 0 0 0 x x x
0 0 0 1 x x x
0 0 0 0 x x x
0 0 0 1 x x x
0 0 0 0 x x x
0 0 0 1 x x x
0 0 0 0 x x x
0 0 0 1 x x x
0 0 0 0 x x x
0 0 0 1 x x x
0 0 0 0 x x x
0 0 0 1 x x x
0 0 0 0 x x x
0 0 0 1 x x x
0 0 0 0 x x x
0 0 0 1 x x x
0 0 0 0 x x x
0 0 0 1 x x x
0 0 0 0 x x x
0 0 0 1 x x x
0 0 0 0 x x x
0 0 0 1 x x x
0 0 0 0 x x x
0 0 0 1 x x x
0 0 0 0 x x x
0 0 0 1 x x x
0 0 0 0 x x x
0 0 0 1 x x x
0 0 0 0 x x x
0 0 0 1 x x x
0 0 0 0 x x x
0 0 0 1 x x x
0 0 0 0 x x x
0 0 0 1 x x x
0 0 0 0 x x x
0 0 0 1 x x x
0 0 0 0 x x x
0 0 0 1 x x x
0 0 0 0 x x x
0 0 0 1 x x x
0 0 0 0 x x x
0 0 0 1 x x x
0 0 0 0 x x x
0 0 0 1 x x x
0 0 0 0 x x x
0 0 0 1 x x x
0 0 0 0 x x x
0 0 0 1 x x x
0 0 0 0 x x x
0 0 0 1 x x x
0 0 0 0 x x x
0 0 0 1 x x x
0 0 0 0 x x x
0 0 0 1 x x x
0 0 0 0 x x x
0 0 0 1 x x x
0 0 0 0 2 154 0
0 0 0 1 2 154 0
122 1 0 0 x x x
122 1 0 1 x x x
0 0 0 0 x x x
0 0 0 1 x x x
0 0 0 0 x x x
0 0 0 1 x x x
0 0 0 0 x x x
0 0 0 1 x x x
0 0 0 0 x x x
0 0 0 1 x x x
0 0 0 0 x x x
0 0 0 1 x x x
0 0 0 0 x x x
0 0 0 1 x x x
0 0 0 0 x x x
0 0 0 1 x x x
0 0 0 0 x x x
0 0 0 1 x x x
0 0 0 0 x x x
0 0 0 1 x x x
0 0 0 0 x x x
0 0 0 1 x x x
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*/
