// Digital circuit 2_08.dig as structural Verilog
module _2_08 (
  input  X0,
  input  X1,
  input  Selector,
  output Z
);

  wire not_3_out, or_1_out, or_2_out;

  // Not not_1 has open pins: in=X0, out=open
  // Not not_2 has open pins: in=X1, out=open
  not not_3 (not_3_out, Selector);
  or or_1 (or_1_out, Selector, X0);
  or or_2 (or_2_out, not_3_out, X1);
  and and_1 (Z, or_1_out, or_2_out);
endmodule
